# Fritzing sketch Board (saved by Fritzing 0.9.10b)
breadboards: 1

parts:
  U1 = ESP32S-HiLetgo [part_number=ESP32S-HiLetgo]
  HC-SR04_Sensor_1 = HC-SR04 Ultrasonic Distance Sensor
  microSD1 = MicroSD Card Module
  LCD1 = LCD screen
  S1 = Pushbutton [package="[THT]"]
  R1 = Trimmer Potentiometer [maximum_resistance=10kΩ knob_status=50% power=0.5W package=THT]
  R2 = Resistor [tolerance=±5% power=0.25 resistance=220 package=THT]
  ZS-042_RTC1 = ZS-042 RTC Module

nets:
  VCC: U1.3.3, HC-SR04_Sensor_1.VCC, microSD1.VCC, S1.Pin_1, S1.Pin_2, ZS-042_RTC1.VCC
  N1: U1.GPIO35, S1.Pin_3, S1.Pin_4, R2.Pin_1
  N2: U1.GPIO32, LCD1.RS
  N3: U1.GPIO33, LCD1.E
  N4: U1.GPIO25, LCD1.DB4
  N5: U1.GPIO26, LCD1.DB5
  N6: U1.GPIO27, LCD1.DB6
  N7: U1.GPIO14, LCD1.DB7
  N8: U1.GPIO12, LCD1.LED+
  GND: U1.GND, HC-SR04_Sensor_1.GND, microSD1.GND, LCD1.VSS, LCD1.LED-, R1.leg2, R2.Pin_0, ZS-042_RTC1.GND
  VIN: U1.VIN, LCD1.VDD, R1.leg1
  N9: U1.GPIO16, HC-SR04_Sensor_1.TRIG
  N10: U1.GPIO17, HC-SR04_Sensor_1.ECHO
  N11: U1.GPIO5, microSD1.CS
  N12: U1.GPIO18, microSD1.SCK
  N13: U1.GPIO19, microSD1.MISO
  N14: U1.GPIO21, ZS-042_RTC1.SDA
  N15: U1.GPIO22, ZS-042_RTC1.SCL
  N16: U1.GPIO23, microSD1.MOSI
  N17: LCD1.V0, R1.wiper

custom parts:
  ESP32S-HiLetgo: HiLetgo ESP-WROOM-32 ESP32 ESP-32S Development Board 2.4GHz Dual-Mode WiFi + Bluetooth Dual Cores Microcontroller The ESP32 integrated with Antenna switches, RF Balun, power amplifiers, low-noise amplifiers, filters, and management modules, and the entire solution occupies the least area of PCB. 2.4 GHz Wi-Fi plus Bluetooth dual-mode chip, with TSMC Ultra-low power consumption 40nm technology,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

// code stored in the sketch: Untitled.ino

